# Fritzing sketch bela-imu-button_bb (saved by Fritzing 0.9.3b)
breadboards: 1

parts:
  Part1 = Bela
  R1 = Resistor [tolerance=±5% resistance=10k package=THT]
  S1 = Pushbutton [package="[THT]"]
  Part2 = 9-DOF Absolute Orientation IMU Fusion Breakout - BNO055

nets:
  N1: Part1.P8_01_GND, R1.Pin_1
  N2: Part1.P9_03_3.3V, S1.Pin_2
  N3: Part1.I2C_3.3V, Part2.3.3V
  N4: Part1.I2C_SCL, Part2.SCL_5V
  N5: Part1.I2C_SDA, Part2.SDA_5V
  N6: Part1.I2C_GND, Part2.GND
  N7: R1.Pin_0, S1.Pin_3, S1.Pin_4

custom parts:
  Bela: Bela low-latency audio/sensor platform
  9-DOF Absolute Orientation IMU Fusion Breakout - BNO055: A MEMS accelerometer, magnetometer and gyroscope on a single die with a high speed ARM Cortex-M0 based processor to digest all the sensor data, abstract the sensor fusion and real time requirements away, and spit out data you can use in quaternions, Euler angles or vectors.
